# Fritzing sketch mqttAirCondition (saved by Fritzing 0.9.3b)
breadboards: 1

parts:
  Raspberry_Pi_1 = Raspberry Pi 3 [part_number=RPI-3-V1.2]
  OLED_I2C1 = OLED 128x64 I2C Monochrome Display
  DHT1 = Humidity and Temperature Sensor DHT11
  パーツ1 = Adafruit CCS811 [part_number="Adafruit #3566"]  # not connected

nets:
  N1: Raspberry_Pi_1.GPIO2, OLED_I2C1.SDA
  N2: Raspberry_Pi_1.GPIO3, OLED_I2C1.SCK
  GND: Raspberry_Pi_1.GND, OLED_I2C1.GND, DHT1.GND_1
  3V3: Raspberry_Pi_1.3V3, DHT1.Vcc
  N3: Raspberry_Pi_1.GPIO14, DHT1.Data-signal
  5V: Raspberry_Pi_1.5V, OLED_I2C1.VDD

custom parts:
  Humidity and Temperature Sensor DHT11: Digital relative humidity & temperature sensor DHT11
  Adafruit CCS811: Breathe easy - we finally have an I2C VOC/eCO2 sensor in the Adafruit shop! Add air quality monitoring to your project and with an Adafruit CCS811 Air Quality Sensor Breakout. This sensor from AMS is a gas sensor that can detect a wide range of Volatile Organic Compounds (VOCs) and is intended for indoor air quality monitoring. When connected to your microcontroller (running our library code)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
